# Fritzing sketch fume-hood (saved by Fritzing 0.9.10b)
breadboards: 1

parts:
  MCU1 = Raspberry Pi Zero
  LED1 = LED - 3mm [color="Green (560nm)" package="3 mm [THT]"]
  Q1 = NPN-Transistor [part_number=2N2222 package="SOT-23 [SMD]"]
  R1 = Resistor [tolerance=±1% power=0.25 resistance=2.2k package=THT]
  F2 = Fan - 4 wire [part_number="noctua NF-A14 industrialppc-3000 PWM" package=THT]
  S2 = SWITCH-MOMENTARY-2 [package=reed_switch_plastic]
  J1 = Power Jack [package=power_jack_slot]
  J2 = Power Jack [package=power_jack_slot]

nets:
  GND: MCU1.pin_6, MCU1.pin_9, MCU1.pin_25, MCU1.pin_30, MCU1.pin_34, MCU1.pin_39, LED1.cathode, Q1.2, F2.GND, S2.1, J1.GNDBREAK, J2.GND
  N1: MCU1.pin_24, R1.Pin_1
  N2: MCU1.pin_32, LED1.anode, S2.2, J2.PWR
  N3: Q1.0, R1.Pin_0
  N4: Q1.1, F2.Tach
  N5: F2.Power, J1.PWR

notes:
  Swtich represents presence sensor. Open when tool is present, closed when tool is removed. Supplying ~2.7V with LED in parallel

custom parts:
  Fan - 4 wire: Fan, 4 wire with tach.
